# Fritzing sketch HM-10 (saved by Fritzing 0.9.3b)

parts:
  Componente1 = Bluetooth HM-10
  Componente2 = Arduino Mega 2560 (Rev3)

nets:
  N1: Componente1.TXD, Componente2.D19/RX1, Componente2.D18/TX1
  GND: Componente1.GND, Componente2.GND
  VCC: Componente1.VCC, Componente2.5V

// code stored in the sketch: HM-10.ino
#include <SoftwareSerial.h>

SoftwareSerial HM10(2, 3); // RX = 2, TX = 3

char appData;  

String inData = "";

void setup()

{

  Serial.begin(9600);

  Serial.println("HM10 serial started at 9600");

  HM10.begin(9600); // set HM10 serial at 9600 baud rate

  pinMode(13, OUTPUT); // onboard LED

  digitalWrite(13, LOW); // switch OFF LED

}

void loop()
{

  HM10.listen();  // listen the HM10 port

  while (HM10.available() > 0) {   // if HM10 sends something then read

    appData = HM10.read();

    inData = String(appData);  // save the data in string format

    Serial.write(appData);

  }

  if (Serial.available()) {           // Read user input if available.

    delay(10);

    HM10.write(Serial.read());

  }
  
}
