# Fritzing sketch MPU6050 (saved by Fritzing 0.9.3b)

parts:
  Componente1 = Arduino Uno (Rev3)
  GY1 = double row female pin header, 10 pins [form="♀ (female)"]

nets:
  N1: Componente1.A2, GY1.pin3
  N2: Componente1.A3, GY1.pin4
  N3: Componente1.5V, GY1.pin1
  N4: Componente1.GND, GY1.pin2

// code stored in the sketch: MPU6050.ino
//C++ code
//Programa: Teste MPU6050 

 //Carrega a biblioteca Wire
#include<Wire.h>
#include <I2Cdev.h>

//Endereco I2C do MPU6050
const int MPU=0x68;

//Variaveis para armazenar valores dos sensores
int AcX,AcY,AcZ,Tmp,GyX,GyY,GyZ;

void setup()
{
  Serial.begin(9600);

  //Inicializa Rotina 
  Wire.begin();
  Wire.beginTransmission(MPU);
  Wire.write(0x6B); 
   
  //Inicializa o MPU-6050
  Wire.write(0); 
  Wire.endTransmission(true);
     
}

void loop()
{
  Wire.beginTransmission(MPU);
  Wire.write(0x3B);  // starting with register 0x3B (ACCEL_XOUT_H)
  Wire.endTransmission(false);
  //Solicita os dados do sensor
  Wire.requestFrom(MPU,14,true);  
  //Armazena o valor dos sensores nas vari?veis correspondentes
  AcX=Wire.read()<<8|Wire.read();  //0x3B (ACCEL_XOUT_H) & 0x3C (ACCEL_XOUT_L)     
  AcY=Wire.read()<<8|Wire.read();  //0x3D (ACCEL_YOUT_H) & 0x3E (ACCEL_YOUT_L)
  AcZ=Wire.read()<<8|Wire.read();  //0x3F (ACCEL_ZOUT_H) & 0x40 (ACCEL_ZOUT_L)
  Tmp=Wire.read()<<8|Wire.read();  //0x41 (TEMP_OUT_H) & 0x42 (TEMP_OUT_L)
  GyX=Wire.read()<<8|Wire.read();  //0x43 (GYRO_XOUT_H) & 0x44 (GYRO_XOUT_L)
  GyY=Wire.read()<<8|Wire.read();  //0x45 (GYRO_YOUT_H) & 0x46 (GYRO_YOUT_L)
  GyZ=Wire.read()<<8|Wire.read();  //0x47 (GYRO_ZOUT_H) & 0x48 (GYRO_ZOUT_L)
   
  //Envia valor X do acelerometro para a serial 
  Serial.print("AcX = "); 
	Serial.print(AcX);

  //Envia valor Y do acelerometro para a serial 
  Serial.print(" | AcY = ");
  Serial.print(AcY);
   
  //Envia valor Z do acelerometro para a serial 
  Serial.print(" | AcZ = "); 
	Serial.print(AcZ);
   
  //Envia valor da temperatura para a serial 
  //Calcula a temperatura em graus Celsius
  Serial.print(" | Tmp = "); 
	Serial.print(Tmp/340.00+36.53);
 
  //Envia valor X do giroscopio para a serial 
  Serial.print(" | GyX = "); 
	Serial.print(GyX);
   
  //Envia valor Y do giroscopio para a serial 
  Serial.print(" | GyY = "); 
	Serial.print(GyY);
   
  //Envia valor Z do giroscopio para a serial 
  Serial.print(" | GyZ = "); 
	Serial.println(GyZ);
   
  //Aguarda 300 ms e reinicia o processo
  delay(300);
}
